// Logisim project 4-bit adder & 4-bit substractor.circ as structural Verilog: 1 circuit, main circuit main
module main (
  input  A3,
  input  B3,
  input  A2,
  input  B2,
  input  A1,
  input  B1,
  input  A0,
  input  B0,
  input  Ci0,
  input  A3_2,
  input  B3_2,
  input  A2_2,
  input  B2_2,
  input  A1_2,
  input  B1_2,
  input  A0_2,
  input  B0_2,
  input  Ci0_2
);

  wire and_1_out, and_2_out, and_3_out, and_4_out, and_5_out, and_6_out, and_7_out, and_8_out, and_9_out,
       and_10_out, and_11_out, and_12_out, and_13_out, and_14_out, and_15_out, and_16_out, not_1_out,
       not_2_out, not_3_out, not_4_out, or_1_out, or_2_out, or_3_out, or_4_out, or_5_out, or_6_out, or_7_out,
       or_8_out, or_9_out, or_10_out, or_11_out, or_12_out, or_13_out, or_14_out, or_15_out, or_16_out,
       xor_1_out, xor_2_out, xor_3_out, xor_4_out, xor_5_out, xor_6_out, xor_7_out, xor_8_out, xor_9_out,
       xor_10_out, xor_11_out, xor_12_out, xor_13_out, xor_14_out, xor_15_out, xor_16_out;

  and and_1 (and_1_out, A3, B3);
  and and_2 (and_2_out, A3_2, not_1_out);
  or or_1 (or_1_out, A3, B3);
  and and_3 (and_3_out, or_1_out, or_5_out);
  or or_2 (or_2_out, and_1_out, and_3_out);
  LED led_1 (.in(or_2_out));
  or or_3 (or_3_out, A3_2, not_1_out);
  and and_4 (and_4_out, or_3_out, or_7_out);
  or or_4 (or_4_out, and_2_out, and_4_out);
  LED led_2 (.in(or_4_out));
  xor xor_1 (xor_1_out, A3, B3);
  not not_1 (not_1_out, B3_2);
  xor xor_2 (xor_2_out, A3_2, not_1_out);
  xor xor_3 (xor_3_out, xor_2_out, or_7_out);
  LED led_3 (.in(xor_3_out));
  xor xor_4 (xor_4_out, xor_1_out, or_5_out);
  LED led_4 (.in(xor_4_out));
  and and_5 (and_5_out, A2, B2);
  or or_5 (or_5_out, and_5_out, and_7_out);
  or or_6 (or_6_out, A2_2, not_2_out);
  and and_6 (and_6_out, A2_2, not_2_out);
  or or_7 (or_7_out, and_6_out, and_8_out);
  or or_8 (or_8_out, A2, B2);
  and and_7 (and_7_out, or_8_out, or_11_out);
  and and_8 (and_8_out, or_6_out, or_9_out);
  xor xor_5 (xor_5_out, A2, B2);
  xor xor_6 (xor_6_out, xor_5_out, or_11_out);
  LED led_5 (.in(xor_6_out));
  not not_2 (not_2_out, B2_2);
  xor xor_7 (xor_7_out, A2_2, not_2_out);
  xor xor_8 (xor_8_out, xor_7_out, or_9_out);
  LED led_6 (.in(xor_8_out));
  and and_9 (and_9_out, A1, B1);
  and and_10 (and_10_out, A1_2, not_3_out);
  or or_9 (or_9_out, and_10_out, and_12_out);
  or or_10 (or_10_out, A1, B1);
  and and_11 (and_11_out, or_10_out, or_14_out);
  or or_11 (or_11_out, and_9_out, and_11_out);
  or or_12 (or_12_out, A1_2, not_3_out);
  and and_12 (and_12_out, or_12_out, or_16_out);
  xor xor_9 (xor_9_out, A1, B1);
  xor xor_10 (xor_10_out, xor_9_out, or_14_out);
  LED led_7 (.in(xor_10_out));
  not not_3 (not_3_out, B1_2);
  xor xor_11 (xor_11_out, A1_2, not_3_out);
  xor xor_12 (xor_12_out, xor_11_out, or_16_out);
  LED led_8 (.in(xor_12_out));
  and and_13 (and_13_out, A0_2, not_4_out);
  or or_13 (or_13_out, A0, B0);
  and and_14 (and_14_out, A0, B0);
  or or_14 (or_14_out, and_14_out, and_16_out);
  or or_15 (or_15_out, A0_2, not_4_out);
  and and_15 (and_15_out, or_15_out, Ci0_2);
  or or_16 (or_16_out, and_13_out, and_15_out);
  and and_16 (and_16_out, or_13_out, Ci0);
  xor xor_13 (xor_13_out, A0_2, not_4_out);
  xor xor_14 (xor_14_out, A0, B0);
  xor xor_15 (xor_15_out, xor_14_out, Ci0);
  LED led_9 (.in(xor_15_out));
  not not_4 (not_4_out, B0_2);
  xor xor_16 (xor_16_out, xor_13_out, Ci0_2);
  LED led_10 (.in(xor_16_out));

  // Notes on the sheet:
  //   4-bit Adder
  //   4-bit Substractor
  //   Co3
  //   Co3
  //   S3
  //   S3
  //   Ci3
  //   Ci3
  //   Co2
  //   Co2
  //   S2
  //   S2
  //   Ci2
  //   CESAR ANDRES ZULETA MALANCO   ID: 300077
  //   Ci2
  //   Co1
  //   Co1
  //   S1
  //   S1
  //   Ci1
  //   Ci1
  //   Co0
  //   Co0
  //   S0
  //   S0
endmodule
