// Logisim project ALU (Aritmethic Logic Unit).circ as structural Verilog: 1 circuit, main circuit main
module main (
  input  [3:0] A,
  input  [3:0] B,
  input  Sel__0,
  input  Sel__1,
  output Add_Co,
  output Sub_Co,
  output [3:0] Result
);

  wire and_1_out, and_2_out, and_3_out, nor_1_out;
  wire [3:0] adder_1_out, and_4_out, bit_extender_1_out, bit_extender_2_out, bit_extender_3_out,
       bit_extender_4_out, multiplier_1_out, multiplier_2_out, multiplier_3_out, multiplier_4_out, or_1_out,
       subtractor_1_out;

  nor nor_1 (nor_1_out, Sel__0, Sel__1);
  and and_1 (and_1_out, ~Sel__0, Sel__1);  // AND_Gate
  and and_2 (and_2_out, Sel__0, ~Sel__1);  // AND_Gate
  and and_3 (and_3_out, Sel__0, Sel__1);
  assign bit_extender_1_out = {{3{1'b0}}, nor_1_out};  // Bit_Extender bit_extender_1
  assign bit_extender_2_out = {{3{1'b0}}, and_1_out};  // Bit_Extender bit_extender_2
  assign bit_extender_3_out = {{3{1'b0}}, and_2_out};  // Bit_Extender bit_extender_3
  assign bit_extender_4_out = {{3{1'b0}}, and_3_out};  // Bit_Extender bit_extender_4
  Adder #(.width(4)) adder_1 (.a(A), .b(B), .out(adder_1_out), .cout(Add_Co));  // open: cin
  Multiplier #(.width(4)) multiplier_1 (
    .a(adder_1_out), .b(bit_extender_1_out), .out(multiplier_1_out));  // open: cin, cout
  Subtractor #(.width(4)) subtractor_1 (.a(A), .b(B), .out(subtractor_1_out), .bout(Sub_Co));  // open: bin
  Multiplier #(.width(4)) multiplier_2 (
    .a(subtractor_1_out), .b(bit_extender_2_out), .out(multiplier_2_out));  // open: cin, cout
  assign or_1_out = A | B;  // OR_Gate or_1, 4 bits wide
  Multiplier #(.width(4)) multiplier_3 (
    .a(or_1_out), .b(bit_extender_3_out), .out(multiplier_3_out));  // open: cin, cout
  assign and_4_out = A & B;  // AND_Gate and_4, 4 bits wide
  Multiplier #(.width(4)) multiplier_4 (
    .a(and_4_out), .b(bit_extender_4_out), .out(multiplier_4_out));  // open: cin, cout
  assign Result = multiplier_4_out | multiplier_3_out | multiplier_2_out | multiplier_1_out;  // OR_Gate or_2, 4 bits wide

  // Notes on the sheet:
  //   CESAR ANDRES ZULETA MALANCO  ID:300077
  //   Selector
endmodule
