// Logisim project Moore state machine (111 sequence).circ as structural Verilog: 1 circuit, main circuit main
module main (
  input  in_1
);

  wire and_1_out, and_2_out, and_3_out, clock_1_out, d_ff_1_q, d_ff_2_q, d_ff_2_qn, or_1_out, xor_1_out;

  xor xor_1 (xor_1_out, d_ff_1_q, d_ff_2_q);
  or or_1 (or_1_out, d_ff_1_q, d_ff_2_qn);
  and and_1 (and_1_out, in_1, xor_1_out);
  Clock clock_1 (.out(clock_1_out));
  and and_2 (and_2_out, in_1, or_1_out);
  D_Flip_Flop d_ff_1 (.clk(clock_1_out), .D(and_1_out), .Q(d_ff_1_q));  // open: Qn, preset, en, reset
  D_Flip_Flop d_ff_2 (.clk(clock_1_out), .D(and_2_out), .Q(d_ff_2_q), .Qn(d_ff_2_qn));  // open: preset, en, reset
  and and_3 (and_3_out, d_ff_1_q, d_ff_2_q);
  LED led_1 (.in(and_3_out));
endmodule
